# Fritzing sketch Sniffer (saved by Fritzing 0.9.2b)
breadboards: 1

parts:
  U1 = NodeMCU V3.0
  LED2 = smd LED [color="Red (633nm)" package="1206 [SMD]"]
  R1 = Resistor [tolerance=±5% resistance=220 package="2512 [SMD]"]
  S1 = Pushbutton [package="[SMD]"]

nets:
  N1: U1.D2, R1.Pin_1
  N2: U1.D4, S1.Pin_1, S1.Pin_2
  N3: U1.GND#6, U1.GND#13, U1.GND#16, LED2.cathode, S1.Pin_3, S1.Pin_4
  N4: U1.S3, U1.VU
  N5: LED2.anode, R1.Pin_0

notes:
  DHT11
  NovaFitness SDS011
  Reset button

custom parts:
  NodeMCU V3.0: ESP8266 based NodeMCU
